# Fritzing sketch Fritzing-bachir-01 (saved by Fritzing 0.9.3b)
breadboards: 1

parts:
  U1 = LM124-324 Quad Opamp [package="DIP (Dual Inline)"]
  C1 = Ceramic Capacitor [capacitance=100nF package="100 mil [THT, multilayer]"]
  R1 = Resistor [tolerance=±5% resistance=8.2k power=2 package=THT]
  R2 = Resistor [tolerance=±5% resistance=68k package=THT]
  C2 = Ceramic Capacitor [capacitance=1µF package="100 mil [THT, multilayer]"]
  Q1 = LTR-301 [package=ltr-301]
  D1 = LTE-302 [package=lte-302]
  R3 = Resistor [tolerance=±5% resistance=220 package=THT]
  R4 = Resistor [tolerance=±5% resistance=10k package=THT]
  Composant1 = Arduino Ethernet Shield (Rev3)
  C3 = Ceramic Capacitor [capacitance=1µF package="100 mil [THT, multilayer]"]
  R5 = Resistor [tolerance=±5% resistance=68k package=THT]
  R6 = Resistor [tolerance=±5% resistance=1k package=THT]
  C4 = Ceramic Capacitor [capacitance=1µF package="100 mil [THT, multilayer]"]
  R7 = Resistor [tolerance=±5% resistance=470k package=THT]
  R8 = Resistor [tolerance=±5% resistance=1.2k package=THT]
  Q2 = TRANSISTOR_NPN [package=to-92-ammo]

nets:
  N1: U1.1OUT, C1.1, C3.1
  N2: U1.1IN-, U1.VCC+, C1.0, R1.Pin_1
  N3: U1.1IN+, R2.Pin_1, C2.0
  N4: U1.VCC-, R3.Pin_1, R4.Pin_1, Composant1.5V, Q2.C
  N5: U1.4IN+, C3.0, R5.Pin_1
  N6: U1.4IN-, R6.Pin_1, C4.0, R7.Pin_0
  N7: U1.4OUT, C4.1, R7.Pin_1, R8.Pin_0
  N8: R1.Pin_0, R2.Pin_0, Q1.E, D1.C, Composant1.GND
  N9: C2.1, Q1.C, R4.Pin_0
  N10: D1.A, R3.Pin_0
  N11: Composant1.A0, Q2.E
  N12: R5.Pin_0, R6.Pin_0
  N13: R8.Pin_1, Q2.B
