# Fritzing sketch fritzing.modul02 (saved by Fritzing 0.9.3b)
breadboards: 1

parts:
  LED2 = LED - 3mm [color="Red (633nm)" package="3 mm [THT]"]
  LED3 = LED - 3mm [color="Red (633nm)" package="3 mm [THT]"]
  LED4 = LED - 3mm [color="Red (633nm)" package="3 mm [THT]"]
  LED5 = LED - 3mm [color="Red (633nm)" package="3 mm [THT]"]
  LED7 = LED - 3mm [color="Red (633nm)" package="3 mm [THT]"]
  LED10 = LED - 3mm [color="Red (633nm)" package="3 mm [THT]"]
  R3 = Resistor [tolerance=±5% resistance=220 package=THT]
  R4 = Resistor [tolerance=±5% resistance=220 package=THT]
  R7 = Resistor [tolerance=±5% resistance=220 package=THT]
  R10 = Resistor [tolerance=±5% resistance=220 package=THT]
  R12 = Resistor [tolerance=±5% resistance=220 package=THT]
  R13 = Resistor [tolerance=±5% resistance=220 package=THT]
  R14 = Resistor [tolerance=±5% resistance=220 package=THT]
  R15 = Resistor [tolerance=±5% resistance=220 package=THT]
  R16 = Resistor [tolerance=±5% resistance=220 package=THT]
  LED11 = LED - 5mm [color="Red (633nm)" package="5 mm [THT]"]
  LED12 = LED - 5mm [color="Red (633nm)" package="5 mm [THT]"]
  LED13 = LED - 5mm [color="Red (633nm)" package="5 mm [THT]"]
  LED15 = LED - 5mm [color="Red (633nm)" package="5 mm [THT]"]
  R17 = Resistor [tolerance=±5% resistance=220 package=THT]
  Arduino1 = Arduino Uno (Rev3)

nets (from the breadboard view):
  N1: LED2.cathode, LED2.anode, LED3.cathode, LED3.anode, LED4.cathode, LED4.anode, LED5.cathode, LED5.anode, LED7.cathode, LED7.anode, LED10.cathode, LED10.anode, R3.Pin_0, R4.Pin_0, R7.Pin_0, R7.Pin_1, R12.Pin_0, R13.Pin_0, R13.Pin_1, R14.Pin_0, R15.Pin_0, R15.Pin_1, R16.Pin_0, LED11.cathode, LED11.anode, LED12.cathode, LED13.cathode, LED13.anode, LED15.cathode, LED15.anode, R17.Pin_0, Arduino1.D2
  N2: R3.Pin_1, R17.Pin_1
  N3: R4.Pin_1, Arduino1.D8
  N4: R10.Pin_0, Arduino1.D7
  N5: R10.Pin_1, LED12.anode
  N6: R12.Pin_1, Arduino1.D4
